# Fritzing sketch board (saved by Fritzing 0.9.3b)

parts:
  hc-sr1 = hc-sr04
  Mod1 = Arduino Sensor Shield v5.0
  S1 = H-Bridge with L298N
  SERVO1 = Tower Pro SG90 servo [part_number=101246]
  BT1 = Bluetooth HC-06d [package=THT]
  M1 = DC Motor
  J1 = Power Jack [package=power_jack_combo]
  SERVO2 = Tower Pro SG90 servo [part_number=101246]
  SERVO3 = Tower Pro SG90 servo [part_number=101246]
  SERVO4 = Tower Pro SG90 servo [part_number=101246]
  M2 = DC Motor
  M3 = DC Motor
  M4 = DC Motor
  VCC1 = Battery

nets:
  VCC: hc-sr1.VCC, Mod1.VCC, Mod1.A0-VCC, Mod1.COM-VCC, Mod1.12-V, Mod1.ParallelLCD-VCC, SERVO1.+5V, BT1.VCC
  N1: hc-sr1.Trig, Mod1.SD-D13, Mod1.13-S
  N2: hc-sr1.Echo, Mod1.SD-D12, Mod1.12-S
  GND: hc-sr1.GND, Mod1.URF01-GND, Mod1.A0-GND, Mod1.COM-GND, Mod1.12-G, Mod1.ParallelLCD-GND, SERVO1.GND, BT1.GND
  N3: Mod1.URF01-A0, Mod1.A0-SIG, SERVO1.Signal
  N4: Mod1.URF01-A1, Mod1.A1-SIG, SERVO4.Signal
  N5: Mod1.A2-SIG, SERVO3.Signal
  N6: Mod1.A3-SIG, SERVO2.Signal
  N7: Mod1.COM-TX, BT1.RXD
  N8: Mod1.COM-RX, BT1.TXD
  N9: Mod1.7-S, Mod1.ParallelLCD-D7, S1.IN1
  N10: Mod1.6-S, Mod1.ParallelLCD-D6, S1.ENA
  N11: Mod1.5-S, Mod1.ParallelLCD-D5, S1.IN2
  N12: Mod1.4-S, Mod1.ParallelLCD-D4, S1.IN3
  N13: Mod1.3-S, Mod1.ParallelLCD-D3, S1.ENB
  N14: Mod1.2-S, Mod1.ParallelLCD-D2, S1.IN4
  N15: S1.GND, VCC1.-
  N16: S1.M1-01, M3.pin_2, M4.pin_2
  N17: S1.M1-02, M3.pin_1, M4.pin_1
  N18: S1.M2-01, M1.pin_2, M2.pin_2
  N19: S1.M2-02, M1.pin_1, M2.pin_1
  N20: J1.GND, VCC1.+

notes:
  Servo Hông
  Servo Vai
  Servo Khủy tay
  Servo Cánh tay
  Bánh xe trái
  Bánh xe phải
  Sensor Shield
  Servo SG90
  Động cơ DC
  Module điều khiển động cơ L298N
  Nguồn ngoài gồm 2 pin 3.7V
  Giắc cắm nguồn cho Arduino
  Cảm biến siêu âm HC-SR04
  Module thu phát Bluetooth HC06

custom parts:
  Arduino Sensor Shield v5.0: Arduino Sensor Shield v5.0 provides I2C interface, Bluetooth module communication interface, SD card module communication interface, APC220 wireless RF modules communication interface, RB URF V1.1 ultrasonic sensors interface, 12864 LCD serial and parallel interface, 32 servo controller interfaces. In addition (with the sel jumper removed) allows an external power supply for the servos as the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
  H-Bridge with L298N: h-bridge
  Tower Pro SG90 servo: Original file by John De Cristofaro http://www.adafruit.com/products/1449 Adafruit Feedback Servo (Small) Edited by: e-radionica.com 28/9/2015
  Bluetooth HC-06d: Bluetooth HC-06 - face down, pins down 16.5mm x 37.5mm PCB
